# Fritzing sketch netsensor (saved by Fritzing 0.6.5b)
breadboards: 1

parts:
  R1 = Photocell (LDR) [package=THT]
  Arduino1 = Arduino
  R2 = Resistor [tolerance=±5% resistance=10k package=THT]
  T1 = TMP36 Temperature Sensor [package="TO92 [THT]"]

nets:
  GND: R1.pin_0, Arduino1.GND, T1.GND
  N1: R1.pin_1, Arduino1.A1, R2.Pin_0
  N2: Arduino1.+5V, R2.Pin_1, T1.+Vs
  N3: Arduino1.A0, T1.Vout
